# Fritzing sketch sketch (saved by Fritzing 0.9.6b)
circuit board: 8.46667cm x 5.64444cm
breadboards: 1

parts:
  Part1 = Arduino Uno (Rev3)
  R1 = Resistor [tolerance=±5% power=0.25 resistance=220 package=THT]
  LED1 = LED - 5mm [color="Green (570nm)" current=0.030 package="5 mm [THT]"]
  LED2 = LED - 5mm [color="Red (660nm)" current=0.030 package="5 mm [THT]"]
  R2 = Resistor [tolerance=±5% power=0.25 resistance=220 package=THT]
  R3 = Resistor [tolerance=±5% power=0.25 resistance=10k package=THT]
  S1 = Pushbutton [package="[THT]"]
  J1 = Basic Servo
  VCC1 = 4 x AAA Battery Mount

nets:
  N1: Part1.A0, R3.Pin_1, S1.Pin_3, S1.Pin_4
  N2: Part1.D8, LED2.anode
  N3: Part1.D9_PWM, J1.pulse
  N4: Part1.D7, LED1.anode
  N5: Part1.5V, S1.Pin_1, S1.Pin_2
  GND: Part1.GND, R1.Pin_0, R2.Pin_0, R3.Pin_0, J1.gnd, VCC1.-
  N6: R1.Pin_1, LED1.cathode
  N7: LED2.cathode, R2.Pin_1
  N8: J1.vcc, VCC1.+
